# Fritzing sketch nomis (saved by Fritzing 0.9.3b)
breadboards: 1

parts:
  Raspberry_Pi_1 = Raspberry Pi 3 [part_number=RPI-3-V1.2]
  S1 = Pushbutton [package="[THT]"]
  R1 = Resistor [tolerance=±5% resistance=220 package=THT]
  S3 = Pushbutton [package="[THT]"]
  R3 = Resistor [tolerance=±5% resistance=220 package=THT]
  S5 = Pushbutton [package="[THT]"]
  R5 = Resistor [tolerance=±5% resistance=220 package=THT]
  S6 = Pushbutton [package="[THT]"]
  R6 = Resistor [tolerance=±5% resistance=220 package=THT]
  R7 = Resistor [tolerance=±5% resistance=220 package=THT]
  S7 = Pushbutton [package="[THT]"]
  LED1 = LED - 3mm [color="Red (633nm)" package="3 mm [THT]"]
  LED5 = LED - 3mm [color="Green (555nm)" package="3 mm [THT]"]
  LED6 = LED - 3mm [color="Blue (430nm)" package="3 mm [THT]"]
  LED3 = LED - 3mm [color="Yellow (592nm)" package="3 mm [THT]"]
  J1 = Piezo Speaker

nets:
  N1: Raspberry_Pi_1.GIPO17, LED6.anode
  N2: Raspberry_Pi_1.GIPO27, S1.Pin_1, S1.Pin_2, R1.Pin_1
  N3: Raspberry_Pi_1.GIPO22, LED3.anode
  N4: Raspberry_Pi_1.GIPO6, Raspberry_Pi_1.GIPO19, Raspberry_Pi_1.GND, S1.Pin_3, S1.Pin_4, S3.Pin_3, S3.Pin_4, S5.Pin_1, S5.Pin_2, S5.Pin_3, S5.Pin_4, R5.Pin_1, S6.Pin_1, S6.Pin_2, S6.Pin_3, S6.Pin_4, R6.Pin_1, S7.Pin_3, S7.Pin_4, LED1.cathode, LED5.cathode, LED6.cathode, LED3.cathode, J1.pin2
  N5: Raspberry_Pi_1.GIPO26, Raspberry_Pi_1.GIPO21, R7.Pin_1, S7.Pin_1, S7.Pin_2
  N6: Raspberry_Pi_1.GIPO16, LED1.anode
  N7: Raspberry_Pi_1.GIPO12, LED5.anode
  N8: Raspberry_Pi_1.GIPO23, S3.Pin_1, S3.Pin_2, R3.Pin_1
  N9: Raspberry_Pi_1.5V, R1.Pin_0, R3.Pin_0, R5.Pin_0, R6.Pin_0, R7.Pin_0, J1.pin1
